// Logisim project d_flip_flop_divider.circ as structural Verilog: 1 circuit, main circuit main
module main (
  input  CLK,
  output Q,
  output nQ
);

  D_Flip_Flop #(.trigger("rising")) d_ff_1 (.clk(nQ), .D(CLK), .Q(Q), .Qn(nQ));  // open: preset, en, reset
endmodule
