// Logisim project decoder_2to4.circ as structural Verilog: 1 circuit, main circuit main
module main (
  input  a0,
  input  a1,
  output Y0_na1_na0,
  output Y1_na1_a0,
  output Y2__a1_na0,
  output Y3__a1_a0
);

  wire not_1_out;

  not not_1 (not_1_out, a0);
  not not_2 (a1, a1);
  and and_1 (Y0_na1_na0, not_1_out, a1);
  and and_2 (Y1_na1_a0, a0, a1);
  and and_3 (Y2__a1_na0, not_1_out, a1);
  and and_4 (Y3__a1_a0, a0, a1);
endmodule
