// Logisim project matrix_encoder_16to4.circ as structural Verilog: 1 circuit, main circuit main
module main (
  input  X0,
  input  X1,
  input  X2,
  input  X3,
  input  X4,
  input  X5,
  input  X6,
  input  X7,
  input  X8,
  input  X9,
  input  X10,
  input  X11,
  input  X12,
  input  X13,
  input  X14,
  input  X15,
  output Y3__8,
  output Y2__4,
  output Y1__2,
  output Y0__1
);

  or or_1 (Y3__8, X8, X9, X10, X11, X12, X13, X14, X15);
  or or_2 (Y2__4, X4, X5, X6, X7, X12, X13, X14, X15);
  or or_3 (Y1__2, X2, X3, X6, X7, X10, X11, X14, X15);
  or or_4 (Y0__1, X1, X3, X5, X7, X9, X11, X13, X15);
endmodule
