// Logisim project universal_suite.circ as structural Verilog
module Half_Adder (
  input  A,
  input  B,
  output S,
  output C
);

  xor xor_1 (S, A, B);
  and and_1 (C, A, B);
endmodule

module Full_Adder (
  input  A,
  input  B,
  input  Cin,
  output S,
  output Cout
);

  wire and_1_out, and_2_out, xor_1_out;

  xor xor_1 (xor_1_out, A, B);
  and and_1 (and_1_out, A, B);
  xor xor_2 (S, xor_1_out, Cin);
  and and_2 (and_2_out, xor_1_out, Cin);
  or or_1 (Cout, and_1_out, and_2_out);
endmodule

module Half_Subtractor (
  input  A,
  input  B,
  output D,
  output Bout
);

  wire not_1_out;

  not not_1 (not_1_out, A);
  xor xor_1 (D, A, B);
  and and_1 (Bout, not_1_out, B);
endmodule

module Comparator_1Bit (
  input  A,
  input  B,
  output GT,
  output EQ,
  output LT
);

  wire not_1_out, not_2_out;

  not not_1 (not_1_out, A);
  not not_2 (not_2_out, B);
  and and_1 (GT, A, not_2_out);
  xnor xnor_1 (EQ, A, B);
  and and_2 (LT, not_1_out, B);
endmodule

module RS_Latch (
  input  R,
  input  S,
  output Q,
  output NotQ
);

  wire undriven, undriven_2;

  nor nor_1 (Q, R, undriven);
  nor nor_2 (NotQ, undriven_2, S);
endmodule

module Shift_Register_4Bit (
  input  Din,
  output Q0,
  output Q1,
  output Q2,
  output Q3
);

  wire CLK_out, undriven, undriven_2, undriven_3;

  Clock CLK (.out(CLK_out));
  D_Flip_Flop #(.trigger("rising")) d_ff_1 (.clk(Din), .D(undriven), .Q(Q0));  // open: Qn, preset, en, reset
  D_Flip_Flop #(.trigger("rising")) d_ff_2 (.clk(Q0), .D(undriven_2), .Q(Q1));  // open: Qn, preset, en, reset
  D_Flip_Flop #(.trigger("rising")) d_ff_3 (.clk(Q1), .D(undriven_3), .Q(Q2));  // open: Qn, preset, en, reset
  D_Flip_Flop #(.trigger("rising")) d_ff_4 (.clk(Q2), .D(CLK_out), .Q(Q3));  // open: Qn, preset, en, reset
endmodule

module Async_Counter_4Bit (
  output Q0,
  output Q1,
  output Q2,
  output Q3
);

  wire CLK_out, d_ff_1_qn, d_ff_2_qn, d_ff_3_qn, d_ff_4_qn;

  Clock CLK (.out(CLK_out));
  D_Flip_Flop #(.trigger("rising")) d_ff_1 (
    .clk(d_ff_1_qn), .D(CLK_out), .Q(Q0), .Qn(d_ff_1_qn));  // open: preset, en, reset
  D_Flip_Flop #(.trigger("rising")) d_ff_2 (
    .clk(d_ff_2_qn), .D(d_ff_1_qn), .Q(Q1), .Qn(d_ff_2_qn));  // open: preset, en, reset
  D_Flip_Flop #(.trigger("rising")) d_ff_3 (
    .clk(d_ff_3_qn), .D(d_ff_2_qn), .Q(Q2), .Qn(d_ff_3_qn));  // open: preset, en, reset
  D_Flip_Flop #(.trigger("rising")) d_ff_4 (
    .clk(d_ff_4_qn), .D(d_ff_3_qn), .Q(Q3), .Qn(d_ff_4_qn));  // open: preset, en, reset
endmodule

module Demux_1to8 (
  input  DI,
  input  E,
  input  A0,
  input  A1,
  input  A2,
  output Y0,
  output Y1,
  output Y2,
  output Y3,
  output Y4,
  output Y5,
  output Y6,
  output Y7
);

  wire not_1_out, not_2_out, not_3_out;

  not not_1 (not_1_out, A0);
  not not_2 (not_2_out, A1);
  not not_3 (not_3_out, A2);
  and and_1 (Y0, DI, not_3_out, not_2_out, not_1_out, E);
  and and_2 (Y1, DI, not_3_out, not_2_out, A0, E);
  and and_3 (Y2, DI, not_3_out, A1, not_1_out, E);
  and and_4 (Y3, DI, not_3_out, A1, A0, E);
  and and_5 (Y4, DI, A2, not_2_out, not_1_out, E);
  and and_6 (Y5, DI, A2, not_2_out, A0, E);
  and and_7 (Y6, DI, A2, A1, not_1_out, E);
  and and_8 (Y7, DI, A2, A1, A0, E);
endmodule

module Mux_8to1 (
  input  D0,
  input  D1,
  input  D2,
  input  D3,
  input  D4,
  input  D5,
  input  D6,
  input  D7,
  input  A0,
  input  A1,
  input  A2,
  input  E,
  output Y
);

  wire and_1_p3, and_2_p3, and_3_p3, and_4_p3, and_5_p3, and_6_p3, and_7_p3, and_8_p3;

  // NOT_Gate not_1 has open pins: in=A0, out=open
  // NOT_Gate not_2 has open pins: in=A1, out=open
  // NOT_Gate not_3 has open pins: in=A2, out=open
  // AND_Gate and_1: pin names not known; wires that end beside it: D0, D0, and_1_p3
  // AND_Gate and_2: pin names not known; wires that end beside it: D1, D1, and_2_p3
  // AND_Gate and_3: pin names not known; wires that end beside it: D2, D2, and_3_p3
  // AND_Gate and_4: pin names not known; wires that end beside it: D3, D3, and_4_p3
  // AND_Gate and_5: pin names not known; wires that end beside it: D4, D4, and_5_p3
  // AND_Gate and_6: pin names not known; wires that end beside it: D5, D5, and_6_p3
  // AND_Gate and_7: pin names not known; wires that end beside it: D6, D6, and_7_p3
  // AND_Gate and_8: pin names not known; wires that end beside it: D7, D7, and_8_p3
  or or_1 (Y, and_1_p3, and_2_p3, and_3_p3, and_4_p3, and_5_p3, and_6_p3, and_7_p3, and_8_p3);
endmodule
